# Fritzing sketch Step-3-Breadboard Design (saved by Fritzing 0.9.2b)
breadboards: 1

parts:
  Part1 = Arduino Uno (Rev3)
  R1 = Resistor [tolerance=±5% resistance=220 package=THT]
  LED1 = LED - 5mm [color="Red (633nm)" package="5 mm [THT]"]
  LED2 = LED - 5mm [color="Red (633nm)" package="5 mm [THT]"]
  LED3 = LED - 5mm [color="Red (633nm)" package="5 mm [THT]"]
  LED4 = LED - 5mm [color="Red (633nm)" package="5 mm [THT]"]
  LED5 = LED - 5mm [color="Red (633nm)" package="5 mm [THT]"]
  LED6 = LED - 5mm [color="Red (633nm)" package="5 mm [THT]"]
  R2 = Resistor [tolerance=±5% resistance=220 package=THT]
  R3 = Resistor [tolerance=±5% resistance=220 package=THT]
  R4 = Resistor [tolerance=±5% resistance=220 package=THT]
  R5 = Resistor [tolerance=±5% resistance=220 package=THT]
  R6 = Resistor [tolerance=±5% resistance=220 package=THT]
  S1 = Pushbutton [package="[THT]"]
  R7 = Resistor [tolerance=±5% resistance=10k package=THT]
  PIR1 = PIR sensor
  S2 = Pushbutton [package="[THT]"]
  R10 = Resistor [tolerance=±5% resistance=10k package=THT]
  R11 = Rotary Potentiometer (Small) [maximum_resistance=100kΩ package=THT]
  R12 = Rotary Potentiometer (Small) [maximum_resistance=100kΩ package=THT]

nets:
  N1: Part1.A0, R11.wiper
  N2: Part1.A1, R12.wiper
  N3: Part1.D9_PWM, R4.Pin_0
  N4: Part1.D10_PWM/SS, R5.Pin_0
  N5: Part1.D11_PWM/MOSI, R6.Pin_0
  N6: Part1.D12/MISO, PIR1.SIG
  N7: Part1.D2, S1.Pin_1, S1.Pin_2, R7.Pin_0
  N8: Part1.D3_PWM, R1.Pin_0
  5V: Part1.D4, Part1.5V, S1.Pin_3, S1.Pin_4, PIR1.VDD, S2.Pin_3, S2.Pin_4, R11.leg2, R12.leg2
  N9: Part1.D5_PWM, R2.Pin_0
  N10: Part1.D6_PWM, R3.Pin_0
  GND: Part1.GND, LED1.cathode, LED2.cathode, LED3.cathode, LED4.cathode, LED5.cathode, LED6.cathode, R7.Pin_1, PIR1.GND, R10.Pin_1, R11.leg1, R12.leg1
  N11: R1.Pin_1, LED1.anode
  N12: LED2.anode, R2.Pin_1
  N13: LED3.anode, R3.Pin_1
  N14: LED4.anode, R4.Pin_1
  N15: LED5.anode, R5.Pin_1
  N16: LED6.anode, R6.Pin_1
  N17: S2.Pin_1, S2.Pin_2, R10.Pin_0
